# Fritzing sketch Obscure (saved by Fritzing 0.9.3b)
breadboards: 1

parts:
  Part1 = Arduino Uno (Rev3)
  Q1 = Basic FET N-Channel [package="TO220 [THT]"]
  SONAR1 = Maxbotix MaxSonar Ultrasonic Sensor (Hi-Res)

nets:
  N1: Part1.D8, Q1.gate
  N2: Part1.D9_PWM, SONAR1.PW
  GND: Part1.GND, Q1.source, SONAR1.GND
  5V: Part1.5V, SONAR1.+5V

notes:
  ESG Privacy Glass HD-1 Volt-Free Connection
  Maxbotix Ultrasonic XL-EZ4
  FQP30N06L

custom parts:
  Maxbotix MaxSonar Ultrasonic Sensor (Hi-Res): Maxbotix MaxSonar Hi-Resolution Ultrasonic Sensor HRLV-EZ0, HRLV-EZ1, HRLV-EZ2, HRLV-EZ3, HRLV-EZ4
